# Fritzing sketch Bedwarmer (saved by Fritzing 1.0.0d)
circuit board: 8.46667cm x 5.64444cm

parts:
  Temp_+ = Momentary Switch [package=ksa_sealed_tac_switch]
  Timer_+ = Momentary Switch [package=ksa_sealed_tac_switch]
  Timer_- = Momentary Switch [package=ksa_sealed_tac_switch]
  Temp_- = Momentary Switch [package=ksa_sealed_tac_switch]
  M1 = DOIT Esp32 DevKit v1 (30 pins long, 11 pins width) [part_number=ESP32S-PIN30]
  Pulldown_Reistor = Resistor [tolerance=±5% power=0.25W resistance=10k package=THT]
  Load_(Heated_Sheets) = Inductor [current=1A inductance=0H package="400 mil [THT]"]
  Power = Momentary Switch [package=ksa_sealed_tac_switch]
  OLED_I2C2 = OLED 128x64 I2C Monochrome Display
  Part1 = Solid State Relay Module (High Level Trigger) [package=relay]
  5V/700mA_DC_PSU = generic-ac-power-supply [package=THT]

nets:
  N1: Temp_+.1, M1.D13
  N2: Temp_+.4, Timer_+.4, Power.3
  N3: Timer_+.1, M1.D14
  N4: Timer_-.1, M1.D27
  N5: Timer_-.3, Temp_-.3, Power.4
  N6: Temp_-.1, M1.D12
  N7: Temp_-.4, Pulldown_Reistor.Pin_1
  3V3: M1.3V3, OLED_I2C2.VDD
  GND: M1.GND, Pulldown_Reistor.Pin_0, OLED_I2C2.GND, Part1.DC-, 5V/700mA_DC_PSU.pin3#2
  N8: M1.D21, OLED_I2C2.SDA
  N9: M1.D22, OLED_I2C2.SCL
  N10: M1.D23, Part1.CH1
  N11: M1.D26, Power.1
  N12: M1.VIN, Part1.DC+, 5V/700mA_DC_PSU.pin3#3
  N13: Load_(Heated_Sheets).pin_0, 5V/700mA_DC_PSU.pin2
  N14: Load_(Heated_Sheets).pin_1, Part1.AC2
  N15: Part1.AC1, 5V/700mA_DC_PSU.pin1

custom parts:
  DOIT Esp32 DevKit v1 (30 pins long, 11 pins width): The DOIT Esp32 DevKit v1 is one of the development board created by DOIT to evaluate the ESP-WROOM-32 module. It is based on the ESP32 microcontroller that boasts Wifi, Bluetooth, Ethernet and Low Power support all in a single chip. (vanepp) made breadboard work, adjusted pin numbering and labels and reduced size of schematic and cleaned up pcb. This chip is 30pins long (2 x15) and 11 pins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
  Solid State Relay Module (High Level Trigger): 5V Omron solid state relay 240V 2A output with resistance fuse.
  generic-ac-power-supply: Generic ac power supply module. Use as is, or customize the svgs to fit your particular device (as they are all different.) Provides AC input and single DC output. PCB is generic and will need modifications if you intend to do a pcb mount.
